# Fritzing sketch banana (saved by Fritzing 0.9.4)
circuit board: 8.47653cm x 6.57095cm
breadboards: 1

parts:
  S1 = 9-pin-tube-socket
  C4 = Electrolytic Capacitor [capacitance=220µF package="100 mil [THT, electrolytic]"]
  12V = female pin header, 2 pins [form="♀ (female)"]
  OUT = Audio Jack (TRS) 3.5mm [package="4Ucon 08780 [THT]"]
  R10 = Resistor [tolerance=±5% resistance=22 package=THT]
  IN = Audio Jack (TRS) 3.5mm [package="4Ucon 08780 [THT]"]
  C5 = Electrolytic Capacitor [capacitance=220µF package="100 mil [THT, electrolytic]"]
  S1out = female pin header, 1 pin [form="♀ (female)"]
  R5 = Resistor [tolerance=±5% resistance=1k package=THT]
  R9 = Resistor [tolerance=±5% resistance=15k package=THT]
  R4 = Resistor [tolerance=±5% resistance=47k package=THT]
  R2 = Resistor [tolerance=±5% resistance=1M package=THT]
  R3 = Resistor [tolerance=±5% resistance=220k package=THT]
  C1 = Ceramic Capacitor [capacitance=47nF package="200 mil [THT, multilayer]"]
  R6 = Resistor [tolerance=±5% resistance=470k package=THT]
  R8 = Resistor [tolerance=±5% resistance=100k package=THT]
  C3 = Electrolytic Capacitor [capacitance=1µF package="100 mil [THT, electrolytic]"]
  R1 = Resistor [tolerance=±5% resistance=68k package=THT]
  P1 = Rotary Potentiometer (Large) [maximum_resistance=100kΩ package=THT]
  S2 = female pin header, 2 pins [form="♀ (female)"]
  S1ai = female pin header, 1 pin [form="♀ (female)"]
  S1in = female pin header, 1 pin [form="♀ (female)"]
  S1ao = female pin header, 1 pin [form="♀ (female)"]
  S1bi = female pin header, 1 pin [form="♀ (female)"]
  S1bo = female pin header, 1 pin [form="♀ (female)"]
  LED = LEDs [package=led10mm]
  S1led = female pin header, 2 pins [form="♀ (female)"]
  C2 = Electrolytic Capacitor [capacitance=1µF package="100 mil [THT, electrolytic]"]

nets:
  p1: S1.pin_1, R8.Pin_0, C2.+
  p2: S1.pin_2, C1.1, R6.Pin_0
  gnd/p3/p5: S1.pin_3, S1.pin_5, C4.-, 12V.pin2, OUT.Sleeve, IN.Sleeve, C5.-, R9.Pin_1, R4.Pin_1, R2.Pin_1, R6.Pin_1, P1.leg2, S2.pin2, S1led.pin2
  p4: S1.pin_4, C4.+, 12V.pin1, R10.Pin_1
  p6: S1.pin_6, R3.Pin_0, C1.0
  p7: S1.pin_7, R1.Pin_0
  p8: S1.pin_8, R4.Pin_0, C3.+
  N1: OUT.Ring, S1out.pin1
  N2: R10.Pin_0, C5.+, R5.Pin_0, R3.Pin_1, R8.Pin_1
  N3: IN.Ring, S1in.pin1
  N4: R5.Pin_1, LED.A
  N5: R9.Pin_0, C3.-, S2.pin1
  N6: R2.Pin_0, R1.Pin_1, S1ai.pin1
  N7: P1.leg1, C2.-
  N8: P1.wiper, S1ao.pin1
  bypass: S1bi.pin1, S1bo.pin1
  N9: LED.C, S1led.pin1

custom parts:
  9-pin-tube-socket: 9 pin tube socket.
