# Fritzing sketch board (saved by Fritzing 0.9.4)
circuit board: 7.9024cm x 6.66552cm
breadboards: 1

parts:
  J1 = female pin header, 31 pins [form="♀ (female)"]  # not connected
  J2 = female pin header, 26 pins [form="♀ (female)"]  # not connected
  R12 = Resistor [tolerance=±5% resistance=1k package=THT]
  LED1 = female pin header, 1 pin [form="♀ (female)"]
  R13 = Resistor [tolerance=±5% resistance=560 package=THT]
  R14 = Resistor [tolerance=±5% resistance=100 package=THT]
  Q2 = NPN-Transistor [package="TO92 [THT]"]
  R15 = Resistor [tolerance=±5% resistance=120k package=THT]
  R16 = Resistor [tolerance=±5% resistance=100k package=THT]
  R17 = Resistor [tolerance=±5% resistance=1k package=THT]
  R18 = Resistor [tolerance=±5% resistance=22k package=THT]
  R19 = Resistor [tolerance=±5% resistance=2.4k package=THT]
  R20 = Resistor [tolerance=±5% resistance=6.8k package=THT]
  C9 = Electrolytic Capacitor [capacitance=47µF package="100 mil [THT, electrolytic]"]
  C12 = Electrolytic Capacitor [capacitance=47µF package="100 mil [THT, electrolytic]"]
  R21 = Resistor [tolerance=±5% resistance=47k package=THT]
  R22 = female pin header, 2 pins [form="♀ (female)"]
  R23 = TRIMPOT [package=3362u-2]
  R24 = Resistor [tolerance=±5% resistance=1k package=THT]
  LED2 = female pin header, 1 pin [form="♀ (female)"]
  Q3 = NPN-Transistor [package="TO92 [THT]"]
  R25 = Resistor [tolerance=±5% resistance=1M package=THT]
  R26 = Resistor [tolerance=±5% resistance=470k package=THT]
  R27 = Resistor [tolerance=±5% resistance=3.9k package=THT]
  C16 = Electrolytic Capacitor [capacitance=47µF package="100 mil [THT, electrolytic]"]
  p9 = female pin header, 1 pin [form="♀ (female)"]
  p10 = female pin header, 1 pin [form="♀ (female)"]
  p11 = female pin header, 1 pin [form="♀ (female)"]
  p12 = female pin header, 1 pin [form="♀ (female)"]
  p13 = female pin header, 1 pin [form="♀ (female)"]
  LED3 = female pin header, 1 pin [form="♀ (female)"]
  out3 = female pin header, 1 pin [form="♀ (female)"]
  S3i1 = female pin header, 2 pins [form="♀ (female)"]
  S3o1 = female pin header, 2 pins [form="♀ (female)"]
  S3in1 = female pin header, 1 pin [form="♀ (female)"]
  S3out1 = female pin header, 1 pin [form="♀ (female)"]
  C18 = Electrolytic Capacitor [capacitance=1µF package="100 mil [THT, electrolytic]"]
  in3 = female pin header, 1 pin [form="♀ (female)"]
  S3 = female pin header, 2 pins [form="♀ (female)"]
  C19 = Electrolytic Capacitor [capacitance=220µF package="100 mil [THT, electrolytic]"]
  12V2 = female pin header, 2 pins [form="♀ (female)"]
  R28 = Resistor [tolerance=±5% resistance=22 package=THT]
  C20 = Electrolytic Capacitor [capacitance=220µF package="100 mil [THT, electrolytic]"]
  R29 = Resistor [tolerance=±5% resistance=1k package=THT]
  R30 = Resistor [tolerance=±5% resistance=15k package=THT]
  R31 = Resistor [tolerance=±5% resistance=47k package=THT]
  R32 = Resistor [tolerance=±5% resistance=1M package=THT]
  R33 = Resistor [tolerance=±5% resistance=220k package=THT]
  R34 = Resistor [tolerance=±5% resistance=470k package=THT]
  R35 = Resistor [tolerance=±5% resistance=100k package=THT]
  C21 = Electrolytic Capacitor [capacitance=10µF package="100 mil [THT, electrolytic]"]
  R36 = Resistor [tolerance=±5% resistance=68k package=THT]
  C1a1 = Film/Foil Capacitor [capacitance=100nF voltage=35V package="5mm [THT, pp]"]
  C1b1 = Film/Foil Capacitor [capacitance=100nF voltage=35V package="5mm [THT, pp]"]
  C17 = Film/Foil Capacitor [capacitance=100nF voltage=35V package="5mm [THT, pp]"]
  C15 = Film/Foil Capacitor [capacitance=100nF voltage=35V package="5mm [THT, pp]"]
  C14 = Film/Foil Capacitor [capacitance=100nF voltage=35V package="5mm [THT, pp]"]
  C11 = Film/Foil Capacitor [capacitance=100nF voltage=35V package="5mm [THT, pp]"]
  C13 = Film/Foil Capacitor [capacitance=100nF voltage=35V package="5mm [THT, pp]"]
  in1 = female pin header, 1 pin [form="♀ (female)"]
  out1 = female pin header, 1 pin [form="♀ (female)"]
  out2 = female pin header, 1 pin [form="♀ (female)"]
  in2 = female pin header, 1 pin [form="♀ (female)"]
  C10 = Film/Foil Capacitor [capacitance=100nF voltage=35V package="5mm [THT, pp]"]
  R37 = Resistor [tolerance=±5% resistance=620 package=THT]

nets:
  12Vreg: R12.Pin_0, R14.Pin_1, R24.Pin_0, R28.Pin_0, C20.+, R29.Pin_0, R33.Pin_1, R35.Pin_1
  N1: R12.Pin_1, LED1.pin1
  9V: R13.Pin_0, R14.Pin_0, R16.Pin_0, R20.Pin_1, C9.+, R22.pin1, R26.Pin_0, R37.Pin_0
  gnd/p3/p5: R13.Pin_1, R15.Pin_0, R18.Pin_0, R19.Pin_0, C9.-, C12.-, R21.Pin_0, R23.CCW, R25.Pin_0, R27.Pin_0, C16.-, S3.pin2, C19.-, 12V2.pin2, C20.-, R30.Pin_1, R31.Pin_1, R32.Pin_1, R34.Pin_1, C13.-, R37.Pin_1
  N2: Q2.E, R19.Pin_1, C12.+, C10.+
  N3: Q2.B, R17.Pin_1, R18.Pin_1, C10.-
  N4: Q2.C, R20.Pin_0, C14.-
  N5: R15.Pin_1, C11.-, in1.pin1
  N6: R16.Pin_1, R17.Pin_0, C11.+
  N7: R21.Pin_1, C14.+, C13.+, out1.pin1
  N8: R22.pin2, Q3.C, C17.-
  N9: R23.WIPER, Q3.B, R26.Pin_1, C15.+
  N10: R24.Pin_1, LED2.pin1
  N11: Q3.E, R27.Pin_1, C16.+
  N12: R25.Pin_1, C15.-, in2.pin1
  N13: p9.pin1, R36.Pin_0
  N14: p10.pin1, R31.Pin_0, C21.+
  N15: p11.pin1, S3in1.pin1, R33.Pin_0
  N16: p12.pin1, S3out1.pin1, R34.Pin_0
  N17: p13.pin1, C18.+, R35.Pin_0
  N18: LED3.pin1, R29.Pin_1
  N19: out3.pin1, C18.-
  N20: S3i1.pin1, C1a1.-
  N21: S3i1.pin2, C1b1.-
  N22: S3o1.pin1, C1a1.+
  N23: S3o1.pin2, C1b1.+
  N24: in3.pin1, R32.Pin_0, R36.Pin_1
  N25: S3.pin1, R30.Pin_0, C21.-
  p4: C19.+, 12V2.pin1, R28.Pin_1
  N26: C17.+, out2.pin1

notes:
  Connection to 12V for LED2
  Connecting GND
