# Fritzing sketch germanium (saved by Fritzing 0.9.4)
circuit board: 3.83055cm x 2.39737cm
breadboards: 1

parts:
  Q1 = NPN-Transistor [package="TO92 [THT]"]
  R2 = Resistor [tolerance=±5% resistance=1M package=THT]
  R3 = Resistor [tolerance=±5% resistance=470k package=THT]
  R6 = Resistor [tolerance=±5% resistance=3.9k package=THT]
  C3 = Ceramic Capacitor [capacitance=5nF package="100 mil [THT, multilayer]"]
  C6 = Electrolytic Capacitor [capacitance=47µF package="100 mil [THT, electrolytic]"]
  C7 = Ceramic Capacitor [capacitance=10nF package="100 mil [THT, multilayer]"]
  9V = female pin header, 2 pins [form="♀ (female)"]
  in = female pin header, 2 pins [form="♀ (female)"]
  out = female pin header, 2 pins [form="♀ (female)"]
  R11 = Resistor [tolerance=±5% resistance=750 package=THT]
  LED = female pin header, 1 pin [form="♀ (female)"]
  R7 = female pin header, 2 pins [form="♀ (female)"]
  R5 = TRIMPOT [package=3362u-2]

nets:
  N1: Q1.E, R6.Pin_1, C6.+
  N2: Q1.B, R3.Pin_1, C3.0, R5.WIPER
  N3: Q1.C, C7.1, R7.pin2
  N4: R2.Pin_0, R6.Pin_0, C6.-, 9V.pin2, in.pin1, out.pin2, R5.CCW
  N5: R2.Pin_1, C3.1, in.pin2
  N6: R3.Pin_0, 9V.pin1, R11.Pin_0, R7.pin1
  N7: C7.0, out.pin1
  N8: R11.Pin_1, LED.pin1
