# Fritzing sketch hfe-NPN (saved by Fritzing 0.9.9b)
breadboards: 1

parts:
  VCC1 = Battery block 9V
  R1 = Resistor [tolerance=±5% resistance=2472 package=THT]
  S1 = Pushbutton [package="[THT]"]
  R2 = Resistor [tolerance=±5% resistance=2.2M package=THT]
  NPN = NPN-Transistor [package="TO92 [THT]"]

nets:
  GND: VCC1.-, NPN.E
  N1: VCC1.+, R1.Pin_1, R2.Pin_1
  Vprobe: R1.Pin_0, NPN.C
  N2: S1.Pin_1, S1.Pin_2, NPN.B
  N3: S1.Pin_3, S1.Pin_4, R2.Pin_0

notes:
  C  B  E
