# Fritzing sketch hfe-PNP (saved by Fritzing 0.9.9b)
breadboards: 1

parts:
  VCC1 = Battery block 9V
  PNP = PNP-Transistor [package="TO92 [THT]"]
  R1 = Resistor [tolerance=±5% resistance=2472 package=THT]
  S1 = Pushbutton [package="[THT]"]
  R2 = Resistor [tolerance=±5% resistance=2.2M package=THT]

nets:
  GND: VCC1.-, R1.Pin_0, R2.Pin_0
  N1: VCC1.+, PNP.E
  N2: PNP.B, S1.Pin_1, S1.Pin_2
  Vprobe: PNP.C, R1.Pin_1
  N3: S1.Pin_3, S1.Pin_4, R2.Pin_1
