# Fritzing sketch silicon (saved by Fritzing 0.9.4)
circuit board: 4.85784cm x 2.66266cm
breadboards: 1

parts:
  R1 = Resistor [tolerance=±5% resistance=100 package=THT]
  Q1 = NPN-Transistor [package="TO92 [THT]"]
  R2 = Resistor [tolerance=±5% resistance=120k package=THT]
  R3 = Resistor [tolerance=±5% resistance=100k package=THT]
  R4 = Resistor [tolerance=±5% resistance=220 package=THT]
  R5 = Resistor [tolerance=±5% resistance=22k package=THT]
  R6 = Resistor [tolerance=±5% resistance=2.4k package=THT]
  R7 = Resistor [tolerance=±5% resistance=6.8k package=THT]
  C1 = Electrolytic Capacitor [capacitance=47µF package="100 mil [THT, electrolytic]"]
  C5 = Ceramic Capacitor [capacitance=1nF package="100 mil [THT, multilayer]"]
  C3 = Ceramic Capacitor [capacitance=10nF package="100 mil [THT, multilayer]"]
  C6 = Electrolytic Capacitor [capacitance=47µF package="100 mil [THT, electrolytic]"]
  C8 = Ceramic Capacitor [capacitance=4.7nF package="100 mil [THT, multilayer]"]
  C7 = Ceramic Capacitor [capacitance=47nF package="100 mil [THT, multilayer]"]
  12V = female pin header, 2 pins [form="♀ (female)"]
  in = female pin header, 2 pins [form="♀ (female)"]
  R9 = Resistor [tolerance=±5% resistance=47k package=THT]
  out = female pin header, 2 pins [form="♀ (female)"]
  R10 = Resistor [tolerance=±5% resistance=300 package=THT]
  R11 = Resistor [tolerance=±5% resistance=1k package=THT]
  LED = female pin header, 1 pin [form="♀ (female)"]
  9V = female pin header, 1 pin [form="♀ (female)"]

nets:
  N1: R1.Pin_0, R3.Pin_0, R7.Pin_1, C1.+, R10.Pin_0, 9V.pin1
  N2: R1.Pin_1, 12V.pin1, R11.Pin_0
  N3: Q1.E, R6.Pin_1, C5.0, C6.+
  N4: Q1.B, R4.Pin_1, R5.Pin_1, C5.1
  N5: Q1.C, R7.Pin_0, C7.1
  N6: R2.Pin_0, R5.Pin_0, R6.Pin_0, C1.-, C6.-, C8.0, 12V.pin2, in.pin1, R9.Pin_0, out.pin2, R10.Pin_1
  N7: R2.Pin_1, C3.1, in.pin2
  N8: R3.Pin_1, R4.Pin_0, C3.0
  N9: C8.1, C7.0, R9.Pin_1, out.pin1
  N10: R11.Pin_1, LED.pin1
