# Fritzing sketch tube-routing (saved by Fritzing 0.9.4)
circuit board: 7.67795cm x 4.95431cm
breadboards: 1

parts:
  3PDT = NKK M2032SS1W01 3PDT Toggle Switch [package=THT]
  S2 = 9-pin-tube-socket
  LED1 = LEDs [package=led10mm]
  GND = female pin header, 1 pin [form="♀ (female)"]
  12V = female pin header, 1 pin [form="♀ (female)"]
  IN = Audio Jack (TRS) 3.5mm [package="4Ucon 08780 [THT]"]
  OUT = Audio Jack (TRS) 3.5mm [package="4Ucon 08780 [THT]"]
  IN_2 = female pin header, 1 pin [form="♀ (female)"]
  OUT_2 = female pin header, 1 pin [form="♀ (female)"]
  LED = female pin header, 1 pin [form="♀ (female)"]
  p1 = female pin header, 1 pin [form="♀ (female)"]
  p2 = female pin header, 1 pin [form="♀ (female)"]
  p6 = female pin header, 1 pin [form="♀ (female)"]
  p7 = female pin header, 1 pin [form="♀ (female)"]
  p8 = female pin header, 1 pin [form="♀ (female)"]

nets:
  N1: 3PDT.L1-1, IN_2.pin1
  N2: 3PDT.C1, IN.Tip
  N3: 3PDT.L1-2, 3PDT.L2-2
  N4: 3PDT.L2-1, OUT_2.pin1
  N5: 3PDT.C2, OUT.Tip
  GND: 3PDT.L3-1, S2.pin_3, S2.pin_5, GND.pin1, IN.Sleeve, OUT.Sleeve
  N6: 3PDT.C3, LED1.C
  N7: S2.pin_1, p1.pin1
  N8: S2.pin_2, p2.pin1
  N9: S2.pin_4, 12V.pin1
  N10: S2.pin_6, p6.pin1
  N11: S2.pin_7, p7.pin1
  N12: S2.pin_8, p8.pin1
  N13: LED1.A, LED.pin1

custom parts:
  NKK M2032SS1W01 3PDT Toggle Switch: NKK M2032SS1W01 3PDT Toggle Switch This switch has three poles and two position
  9-pin-tube-socket: 9 pin tube socket.
