# Fritzing sketch tube (saved by Fritzing 0.9.4)
circuit board: 4.37445cm x 3.7807cm
breadboards: 1

parts:
  C4 = Electrolytic Capacitor [capacitance=220µF package="100 mil [THT, electrolytic]"]
  R10 = Resistor [tolerance=±5% resistance=22 package=THT]
  C5 = Electrolytic Capacitor [capacitance=220µF package="100 mil [THT, electrolytic]"]
  R5 = Resistor [tolerance=±5% resistance=1k package=THT]
  R9 = Resistor [tolerance=±5% resistance=15k package=THT]
  R4 = Resistor [tolerance=±5% resistance=47k package=THT]
  R2 = Resistor [tolerance=±5% resistance=1M package=THT]
  R3 = Resistor [tolerance=±5% resistance=220k package=THT]
  R6 = Resistor [tolerance=±5% resistance=470k package=THT]
  R8 = Resistor [tolerance=±5% resistance=100k package=THT]
  C3 = Electrolytic Capacitor [capacitance=1µF package="100 mil [THT, electrolytic]"]
  R1 = Resistor [tolerance=±5% resistance=68k package=THT]
  S2 = female pin header, 2 pins [form="♀ (female)"]
  in = female pin header, 1 pin [form="♀ (female)"]
  C2 = Electrolytic Capacitor [capacitance=1µF package="100 mil [THT, electrolytic]"]
  S3i = female pin header, 2 pins [form="♀ (female)"]
  S3o = female pin header, 2 pins [form="♀ (female)"]
  S3in = female pin header, 1 pin [form="♀ (female)"]
  S3out = female pin header, 1 pin [form="♀ (female)"]
  C1b = Ceramic Capacitor [capacitance=200pF package="100 mil [THT, multilayer]"]
  C1a = Ceramic Capacitor [capacitance=47nF package="100 mil [THT, multilayer]"]
  12V = female pin header, 2 pins [form="♀ (female)"]
  p1 = female pin header, 1 pin [form="♀ (female)"]
  p2 = female pin header, 1 pin [form="♀ (female)"]
  p6 = female pin header, 1 pin [form="♀ (female)"]
  p8 = female pin header, 1 pin [form="♀ (female)"]
  p7 = female pin header, 1 pin [form="♀ (female)"]
  LED = female pin header, 1 pin [form="♀ (female)"]
  out = female pin header, 1 pin [form="♀ (female)"]

nets:
  gnd/p3/p5: C4.-, C5.-, R9.Pin_1, R4.Pin_1, R2.Pin_1, R6.Pin_1, S2.pin2, 12V.pin2
  p4: C4.+, R10.Pin_1, 12V.pin1
  N1: R10.Pin_0, C5.+, R5.Pin_0, R3.Pin_1, R8.Pin_1
  N2: R5.Pin_1, LED.pin1
  N3: R9.Pin_0, C3.-, S2.pin1
  N4: R4.Pin_0, C3.+, p8.pin1
  N5: R2.Pin_0, R1.Pin_1, in.pin1
  N6: R3.Pin_0, S3in.pin1, p6.pin1
  N7: R6.Pin_0, S3out.pin1, p2.pin1
  N8: R8.Pin_0, C2.+, p1.pin1
  N9: R1.Pin_0, p7.pin1
  N10: C2.-, out.pin1
  N11: S3i.pin1, C1a.0
  N12: S3i.pin2, C1b.0
  N13: S3o.pin1, C1a.1
  N14: S3o.pin2, C1b.1
