# Fritzing sketch breadboard (saved by Fritzing 0.9.9b)
breadboards: 1

parts:
  Part1 = Arduino Uno (Rev3)
  Q1 = Basic FET N-Channel [part_number=IRLZ34N package="TO220 [THT]"]
  R1 = Resistor [tolerance=±5% resistance=1k package=THT]
  R2 = Resistor [tolerance=±5% resistance=1M package=THT]
  Q2 = PNP-Transistor [part_number=BD140 package="TO92 [THT]"]
  R3 = Resistor [tolerance=±5% resistance=27k package=THT]
  R4 = Resistor [tolerance=±5% resistance=1M package=THT]
  Vdisp = female pin header, 1 pin [form="♀ (female)"]
  R5 = Resistor [tolerance=±5% resistance=470 package=THT]
  Power_plug2 = Power plug
  R6 = Resistor [tolerance=±5% resistance=2.2k package=THT]
  D1 = Zener Diode [part_number=24V breakdown_voltage=24V package="300 mil [THT]"]
  C1 = Electrolytic Capacitor [capacitance=10µF voltage=35V package="100 mil [THT, electrolytic]"]
  Q3 = NPN-Transistor [part_number=BD139 package="TO92 [THT]"]
  R7 = Resistor [tolerance=±5% resistance=22k package=THT]
  CT = female pin header, 1 pin [form="♀ (female)"]
  D2 = Zener Diode [part_number=4.7V breakdown_voltage=4.7V package="300 mil [THT]"]
  U1 = Voltage Regulator - 5V [package="TO220 [THT]"]
  C2 = Ceramic Capacitor [capacitance=100nF voltage=35V package="100 mil [THT, multilayer]"]
  C3 = Electrolytic Capacitor [capacitance=2.2µF voltage=35V package="100 mil [THT, electrolytic]"]

nets:
  Vdon: Part1.D8, R1.Pin_0
  5V: Part1.5V, U1.output_voltage, C2.0
  GND: Part1.GND, Q1.source, R2.Pin_1, Power_plug2.GND, D1.anode, C1.-, D2.anode, U1.GND, C2.1, C3.-
  N1: Q1.gate, R1.Pin_1, R2.Pin_0
  N2: Q1.drain, R3.Pin_0
  24V: Q2.E, R4.Pin_0, Q3.E, R7.Pin_1, U1.input_voltage, C3.+
  N3: Q2.B, R3.Pin_1, R4.Pin_1
  N4: Q2.C, R5.Pin_0
  N5: Vdisp.pin1, R5.Pin_1
  34V: Power_plug2.VCC, R6.Pin_0, Q3.C
  N6: R6.Pin_1, D1.cathode, C1.+, Q3.B
  N7: R7.Pin_0, CT.pin1, D2.cathode
